// Logisim project 102_1.circ as structural Verilog: 1 circuit, main circuit main
module main (
  input  [2:0] in_1,
  input  [31:0] in_2,
  input  in_3,
  input  [7:0] in_4,
  input  in_5,
  input  in_6,
  input  [31:0] in_7,
  input  in_8,
  input  in_9,
  output [31:0] out_10
);

  wire clock_1_out, decoder_1_out0, decoder_1_out1, decoder_1_out2, decoder_1_out3, decoder_1_out4,
       decoder_1_out5, decoder_1_out6, decoder_1_out7;
  wire [31:0] adder_1_out, and_1_out, divider_1_out, multiplier_1_out, nand_1_out, or_1_out, register_1_q,
       register_2_q, register_3_q, register_4_q, register_5_q, register_6_q, register_7_q, register_8_q,
       register_9_q, register_10_q, subtractor_1_out, xor_1_out;

  RAM #(.dataWidth(32)) ram_1 (.addr(in_4), .data(in_2), .clk(in_5), .ld(in_6));  // open: sel, clr
  RAM #(.dataWidth(32)) ram_2 (.addr(in_4), .data(in_7), .clk(in_5), .ld(in_6));  // open: sel, clr
  Clock clock_1 (.out(clock_1_out));
  Decoder #(.select(3)) decoder_1 (
    .out0(decoder_1_out0), .out1(decoder_1_out1), .out2(decoder_1_out2), .out3(decoder_1_out3),
    .out4(decoder_1_out4), .out5(decoder_1_out5), .out6(decoder_1_out6), .out7(decoder_1_out7), .sel(in_1),
    .en(in_3));
  Register #(.width(32)) register_1 (.D(in_2), .Q(register_1_q), .clk(in_8));  // open: en, clr
  Register #(.width(32)) register_2 (.D(in_7), .Q(register_2_q), .clk(in_8));  // open: en, clr
  Register #(.width(32)) register_3 (
    .D(register_1_q), .en(decoder_1_out0), .Q(register_3_q), .clk(clock_1_out), .clr(in_9));
  Register #(.width(32)) register_4 (
    .D(register_1_q), .en(decoder_1_out1), .Q(register_4_q), .clk(clock_1_out), .clr(in_9));
  Register #(.width(32)) register_5 (
    .D(register_1_q), .en(decoder_1_out2), .Q(register_5_q), .clk(clock_1_out), .clr(in_9));
  Register #(.width(32)) register_6 (
    .D(register_1_q), .en(decoder_1_out3), .Q(register_6_q), .clk(clock_1_out), .clr(in_9));
  Register #(.width(32)) register_7 (
    .D(register_1_q), .en(decoder_1_out4), .Q(register_7_q), .clk(clock_1_out), .clr(in_9));
  Register #(.width(32)) register_8 (
    .D(register_1_q), .en(decoder_1_out5), .Q(register_8_q), .clk(clock_1_out), .clr(in_9));
  Register #(.width(32)) register_9 (
    .D(register_1_q), .en(decoder_1_out6), .Q(register_9_q), .clk(clock_1_out), .clr(in_9));
  Register #(.width(32)) register_10 (.D(register_1_q), .en(decoder_1_out7), .Q(register_10_q));  // open: clk, clr
  Adder #(.width(32)) adder_1 (.a(register_3_q), .b(register_2_q), .out(adder_1_out));  // open: cin, cout
  Subtractor #(.width(32)) subtractor_1 (
    .a(register_4_q), .b(register_2_q), .out(subtractor_1_out));  // open: bin, bout
  Multiplier #(.width(32)) multiplier_1 (
    .a(register_5_q), .b(register_2_q), .out(multiplier_1_out));  // open: cin, cout
  Divider #(.width(32)) divider_1 (.a(register_6_q), .b(register_2_q), .out(divider_1_out));  // open: upper, rem
  assign xor_1_out = register_7_q ^ register_2_q;  // XOR_Gate xor_1, 32 bits wide
  assign and_1_out = register_8_q & register_2_q;  // AND_Gate and_1, 32 bits wide
  assign or_1_out = register_9_q | register_2_q;  // OR_Gate or_1, 32 bits wide
  assign nand_1_out = ~(register_10_q & register_2_q);  // NAND_Gate nand_1, 32 bits wide
  Multiplexer #(.select(3), .width(32), .enable("false")) multiplexer_1 (
    .in0(adder_1_out), .in1(subtractor_1_out), .in2(multiplier_1_out), .in3(divider_1_out), .in4(xor_1_out),
    .in5(and_1_out), .in6(or_1_out), .in7(nand_1_out), .out(out_10), .sel(in_1));
endmodule
